// Logisim project H1.circ as structural Verilog: 10 circuits, main circuit P1
module P1 (
  input  I2,
  input  I1,
  input  I0,
  output A,
  output B,
  output C,
  output D,
  output E,
  output F,
  output G,
  output H
);

  wire not_1_out, not_2_out, not_3_out, not_4_out, not_5_out, not_6_out, not_7_out, not_8_out, not_9_out,
       not_10_out, not_11_out, not_12_out;

  not not_1 (not_1_out, I0);
  not not_2 (not_2_out, I1);
  not not_3 (not_3_out, I2);
  not not_4 (not_4_out, I1);
  not not_5 (not_5_out, I2);
  not not_6 (not_6_out, I0);
  not not_7 (not_7_out, I2);
  not not_8 (not_8_out, I2);
  not not_9 (not_9_out, I0);
  not not_10 (not_10_out, I1);
  not not_11 (not_11_out, I1);
  not not_12 (not_12_out, I0);
  and and_1 (A, not_1_out, not_2_out, not_3_out);
  and and_2 (B, I0, not_4_out, not_5_out);
  and and_3 (C, not_6_out, I1, not_7_out);
  and and_4 (D, I0, I1, not_8_out);
  and and_5 (E, not_9_out, not_10_out, I2);
  and and_6 (F, I0, not_11_out, I2);
  and and_7 (G, not_12_out, I1, I2);
  and and_8 (H, I0, I1, I2);

  // Notes on the sheet:
  //   PROBLEM 1: DECODER
  //   INPUT SECTION: Do not change anything here!
  //   You may only change the values of the inputs for testing using the hand tool.
  //   Do not introduce any other input or output pins.
  //   To your logic
  //   OUTPUT SECTION: Do not change anything here!
  //   Do not introduce any other input or output pins.
  //   From your logic
endmodule

module P2 (
  input  A,
  input  B,
  input  C,
  output X,
  output Y
);

  wire and_1_out, and_2_out, and_3_out, and_4_out, and_5_out, not_1_out, not_2_out, not_3_out, not_4_out,
       not_5_out, not_6_out;

  not not_1 (not_1_out, C);
  not not_2 (not_2_out, B);
  not not_3 (not_3_out, A);
  not not_4 (not_4_out, A);
  not not_5 (not_5_out, B);
  not not_6 (not_6_out, C);
  and and_1 (and_1_out, not_1_out, not_2_out, not_3_out);
  and and_2 (and_2_out, C, B, not_4_out);
  and and_3 (and_3_out, C, not_5_out, A);
  and and_4 (and_4_out, not_6_out, B, A);
  and and_5 (and_5_out, C, B, A);
  or or_1 (X, and_1_out, and_2_out, and_3_out, and_4_out);
  buf or_2 (Y, and_5_out);  // OR_Gate

  // Notes on the sheet:
  //   PROBLEM 2: PROGRAMMABLE LOGIC ARRAY
  //   INPUT SECTION: Do not change anything here!
  //   You may only change the values of the inputs for testing using the hand tool.
  //   Do not introduce any other input or output pins.
  //   To your logic
  //   OUTPUT SECTION: Do not change anything here!
  //   Do not introduce any other input or output pins.
  //   From your logic
endmodule

module P3 (
  input  A,
  input  B,
  input  C,
  output X
);

  wire transistor_1_out, transistor_2_out, transistor_7_out, transistor_8_out;

  Transistor transistor_1 (.in(transistor_2_out), .out(transistor_1_out), .gate(A));
  Transistor transistor_2 (.in(1'b1), .out(transistor_2_out), .gate(A));
  Transistor transistor_3 (.in(1'b1), .out(transistor_2_out), .gate(C));
  Transistor transistor_4 (.in(transistor_2_out), .out(transistor_1_out), .gate(B));
  Transistor transistor_5 (.in(transistor_1_out), .out(X), .gate(C));
  Transistor transistor_6 (.in(transistor_2_out), .out(transistor_1_out), .gate(C));
  Transistor transistor_7 (.in(1'b1), .out(transistor_7_out), .gate(A));
  Transistor transistor_8 (.in(transistor_7_out), .out(transistor_8_out), .gate(C));
  Transistor transistor_9 (.in(transistor_7_out), .out(X), .gate(B));
  Transistor transistor_10 (.in(transistor_8_out), .out(X), .gate(A));

  // Other names for the same wires on the sheet: tA = A; tB = B; tC = C

  // Notes on the sheet:
  //   PROBLEM 3: SERIES-PARALLEL CIRCUITS OF TRANSISTORS
  //   RESERVED SECTION: Do not change anything here!
  //   You may only change the values of the inputs for testing using the hand tool.
  //   Do not introduce any other input or output pins.
  //   From your pull-down circuit
endmodule

module P4_Main (
  input  A11,
  input  A10,
  input  A9,
  input  A8,
  input  A7,
  input  A6,
  input  A5,
  input  A4,
  input  A3,
  input  A2,
  input  A1,
  input  A0,
  output X11,
  output X10,
  output X9,
  output X8,
  output X7,
  output X6,
  output X5,
  output X4,
  output X3,
  output X2,
  output X1,
  output X0
);


  // Notes on the sheet:
  //   PROBLEM 4: 12-BIT INCREMENTER (Main)
  //   INPUT SECTION: Do not change anything here!
  //   You may only change the values of the inputs for testing using the hand tool.
  //   Do not introduce any other input or output pins.
  //   To your logic
  //   OUTPUT SECTION: Do not change anything here!
  //   Do not introduce any other input or output pins.
  //   From your logic
endmodule

module P4_IncrOneBit (
  input  Cin,
  input  A,
  output S,
  output Cout
);


  // Notes on the sheet:
  //   PROBLEM 4: 12-BIT INCREMENTER (IncrOneBit)
  //   INPUT SECTION: Do not change anything here!
  //   You may only change the values of the inputs for testing using the hand tool.
  //   Do not introduce any other input or output pins.
  //   To your logic
  //   OUTPUT SECTION: Do not change anything here!
  //   Do not introduce any other input or output pins.
  //   From your logic
endmodule

module P4_IncrBit0 (
  input  A,
  output S,
  output Cout
);


  // Notes on the sheet:
  //   PROBLEM 4: 12-BIT INCREMENTER (IncrBit0)
  //   INPUT SECTION: Do not change anything here!
  //   You may only change the values of the inputs for testing using the hand tool.
  //   Do not introduce any other input or output pins.
  //   To your logic
  //   OUTPUT SECTION: Do not change anything here!
  //   Do not introduce any other input or output pins.
  //   From your logic
endmodule

module P5_Main (
  input  A10,
  input  A9,
  input  A8,
  input  A7,
  input  A6,
  input  A5,
  input  A4,
  input  A3,
  input  A2,
  input  A1,
  input  A0,
  output X10,
  output X9,
  output X8,
  output X7,
  output X6,
  output X5,
  output X4,
  output X3,
  output X2,
  output X1,
  output X0
);


  // Notes on the sheet:
  //   PROBLEM 5: 11-BIT LEFT NORMALIZER (Main)
  //   INPUT SECTION: Do not change anything here!
  //   You may only change the values of the inputs for testing using the hand tool.
  //   Do not introduce any other input or output pins.
  //   To your logic
  //   OUTPUT SECTION: Do not change anything here!
  //   Do not introduce any other input or output pins.
  //   From your logic
endmodule

module P5_LSH1 (
  input  [10:0] X,
  output [10:0] Y
);


  // Notes on the sheet:
  //   PROBLEM 5: 11-BIT LEFT NORMALIZER (LSH1)
  //   INPUT SECTION: Do not change anything here!
  //   You may only change the values of the inputs for testing using the hand tool.
  //   Do not introduce any other input or output pins.
  //   To your logic
  //   OUTPUT SECTION: Do not change anything here!
  //   Do not introduce any other input or output pins.
  //   From your logic
endmodule

module P5_Mux11 (
  input  S,
  input  [10:0] A,
  input  [10:0] B,
  output [10:0] X
);


  // Notes on the sheet:
  //   PROBLEM 5: 11-BIT LEFT NORMALIZER (Mux11)
  //   INPUT SECTION: Do not change anything here!
  //   You may only change the values of the inputs for testing using the hand tool.
  //   Do not introduce any other input or output pins.
  //   To your logic
  //   OUTPUT SECTION: Do not change anything here!
  //   Do not introduce any other input or output pins.
  //   From your logic
endmodule

module P5_CLSH1 (
  input  [10:0] X,
  output [10:0] Y
);


  // Notes on the sheet:
  //   PROBLEM 5: 11-BIT LEFT NORMALIZER (CLSH1)
  //   INPUT SECTION: Do not change anything here!
  //   You may only change the values of the inputs for testing using the hand tool.
  //   Do not introduce any other input or output pins.
  //   To your logic
  //   OUTPUT SECTION: Do not change anything here!
  //   Do not introduce any other input or output pins.
  //   From your logic
endmodule
